// Digital circuit UTS_1_1.dig as structural Verilog
module UTS_1_1 (
  input  A,
  input  B,
  input  C
);

  wire and_1_out, and_2_out, and_3_out, and_4_out, and_5_out, nor_1_out, or_1_out, or_2_out;

  and and_1 (and_1_out, A, A);
  and and_2 (and_2_out, A, A);
  and and_3 (and_3_out, A, A);
  or or_1 (or_1_out, A, A, A);
  and and_4 (and_4_out, A, A, A);
  nor nor_1 (nor_1_out, and_1_out, and_2_out, and_3_out);
  and and_5 (and_5_out, nor_1_out, or_1_out);
  or or_2 (or_2_out, and_5_out, and_4_out);
  LED X (.in(or_2_out));

  assign B = A;
  assign C = A;

  // Notes on the sheet:
  //   ARIFA ALFI ZAHRA
  //   (1) (AB + AC + BC)'(A + B + C) + ABC
endmodule
