// Digital circuit UTS_1_11.dig as structural Verilog
module UTS_1_11 (
  input  X,
  input  Y,
  input  Z
);

  wire and_1_out, and_2_out, and_3_out, and_4_out, not_1_out, not_2_out, not_3_out, or_1_out;

  not not_1 (not_1_out, X);
  not not_2 (not_2_out, Z);
  not not_3 (not_3_out, X);
  and and_1 (and_1_out, not_1_out, ~Y, Z);  // And
  and and_2 (and_2_out, X, Y, not_2_out);
  and and_3 (and_3_out, not_3_out, Y, Z);
  and and_4 (and_4_out, X, Y);
  or or_1 (or_1_out, and_1_out, and_2_out, and_3_out, and_4_out);
  LED A (.in(or_1_out));

  // Notes on the sheet:
  //   ARIFA ALFI ZAHRA
  //   (11) x'y'z + xyz' + x'yz + xy
endmodule
